# Fritzing sketch ThermoGun (saved by Fritzing 0.9.3b)

parts:
  Module1 = Ameba RTL8710 Module [package="DIP (Dual Inline) [THT]"]
  Part1 = OLED Monochrome 128x64 0.96 inch [part_number=326]
  S1 = Round Pushbutton
  U1 = MLX90614 [package=to-39]
  U4 = LIPO-1000mAh [package=lipo-1000]
  R1 = Resistor [tolerance=±5% resistance=1k package="2512 [SMD]"]

nets:
  N1: Module1.Vin, U4.+
  N2: Module1.GND#1, U4.-
  N3: Module1.3V3#4, Part1.VIN
  N4: Module1.GND#5, Part1.GND
  N5: Module1.GC1, Part1.SCLK_SCK
  N6: Module1.GC3, Part1.DC_SA0
  N7: Module1.GC0, Part1.RESET
  N8: Module1.GC2, Part1.MOSI_SDA
  N9: Module1.3V3#16, R1.Pin_1
  N10: Module1.GND#17, U1.VSS
  N11: Module1.GC5, U1.SCL_VZ
  N12: Module1.3V3#25, S1.leg1
  N13: Module1.GC4, R1.Pin_0
  N14: Module1.GA5, S1.leg0

custom parts:
  OLED Monochrome 128x64 0.96 inch: These displays are small, only about 1" diameter, but very readable due to the high contrast of an OLED display. This display is made of 128x64 individual white OLED pixels, each one is turned on or off by the controller chip. Because the display makes its own light, no backlight is required. This reduces the power required to run the OLED and is why the display has such high contrast; we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
